// Logisim project DecoderORIcSimulationProject.circ as structural Verilog: 1 circuit, main circuit main
module main (
  input  [2:0] w
);

  wire decoder_1_out0, decoder_1_out1, decoder_1_out2, decoder_1_out3, decoder_1_out4, decoder_1_out5,
       decoder_1_out6, n7432_1_pin3, n7432_1_pin6, n7432_1_pin8, n7432_1_pin11, n7432_2_pin3, n7432_2_pin6,
       n7432_2_pin12;

  Decoder #(.select(3)) decoder_1 (
    .out0(decoder_1_out0), .out1(decoder_1_out1), .out2(decoder_1_out2), .out3(decoder_1_out3),
    .out4(decoder_1_out4), .out5(decoder_1_out5), .out6(decoder_1_out6), .sel(w));  // open: out7, en
  _7432 #(.ShowInternalStructure("true")) u_7432_1 (
    .pin1(decoder_1_out4), .pin2(decoder_1_out5), .pin3(n7432_1_pin3), .pin4(n7432_1_pin3),
    .pin5(decoder_1_out0), .pin6(n7432_1_pin6), .pin13(n7432_1_pin3), .pin12(decoder_1_out3),
    .pin11(n7432_1_pin11), .pin10(decoder_1_out3), .pin9(n7432_1_pin6), .pin8(n7432_1_pin8));
  _7432 #(.ShowInternalStructure("true")) u_7432_2 (
    .pin1(n7432_1_pin11), .pin2(decoder_1_out2), .pin3(n7432_2_pin3), .pin4(n7432_2_pin3),
    .pin5(decoder_1_out1), .pin6(n7432_2_pin6), .pin13(decoder_1_out0), .pin12(n7432_2_pin12),
    .pin11(n7432_1_pin8), .pin10(decoder_1_out6), .pin9(n7432_2_pin6), .pin8(n7432_2_pin12));
  _7_Segment_Display u_7_segment_display_1 (
    .g(decoder_1_out0), .f(n7432_1_pin8), .a(n7432_1_pin8), .b(n7432_1_pin6), .e(n7432_1_pin8),
    .d(n7432_2_pin12), .c(n7432_1_pin6));  // open: dp

  // Notes on the sheet:
  //   x
  //    y
  //   4
  //   5
  //   0
  //   3
  //   3
  //   1
  //   2
  //   a
  //   b,c
  //   0
  //   6
  //   a
  //   f
  //   e
  //   d
  //   0
  //   1
  //   2
  //   3
  //   4
  //   5
  //   6
  //   g
  //   c
  //   b
endmodule
