// Logisim project POS(L).circ as structural Verilog: 1 circuit, main circuit main
module main (
  input  A,
  input  B,
  input  C,
  input  D,
  input  E,
  input  F,
  input  G,
  input  W,
  input  X,
  input  Y,
  input  f_2,
  input  e_2
);

  wire not_1_out, not_2_out, not_3_out, or_1_out, or_2_out, or_3_out, or_4_out;

  not not_1 (not_1_out, W);
  not not_2 (not_2_out, X);
  not not_3 (not_3_out, Y);
  or or_1 (or_1_out, W, not_3_out);
  or or_2 (or_2_out, W, X, not_3_out);
  or or_3 (or_3_out, not_2_out, Y);
  _7_Segment_Display #(.active("false")) u_7_segment_display_1 (
    .g(G), .f(F), .a(A), .b(B), .e(E), .d(D), .c(C));  // open: dp
  and u_a (A, or_2_out, or_3_out);
  and u_c (C, or_1_out, not_2_out);
  or or_4 (or_4_out, W, not_3_out);
  or u_d (D, W, X, Y);
  and u_b (B, or_4_out, not_2_out);
  and u_g (G, not_1_out, not_2_out, not_3_out);

  assign e_2 = E;
  assign f_2 = F;
endmodule
