// Logisim project POS(NOR)(L).circ as structural Verilog: 1 circuit, main circuit main
module main (
  input  A,
  input  B,
  input  C,
  input  D,
  input  E,
  input  F,
  input  G,
  input  W,
  input  X,
  input  Y,
  input  f_2,
  input  e_2
);

  wire nor_1_out, nor_2_out, nor_3_out, nor_4_out, nor_5_out, nor_6_out, nor_7_out, nor_8_out, nor_9_out;

  nor nor_1 (nor_1_out, Y, Y);
  nor nor_2 (nor_2_out, Y, Y);
  nor nor_3 (nor_3_out, X, X);
  nor nor_4 (nor_4_out, W, X, nor_1_out);
  nor nor_5 (nor_5_out, nor_3_out, Y);
  nor nor_6 (nor_6_out, nor_2_out, W);
  _7_Segment_Display #(.active("false")) u_7_segment_display_1 (
    .g(G), .f(F), .a(A), .b(B), .e(E), .d(D), .c(C));  // open: dp
  nor u_a (A, nor_4_out, nor_5_out);
  nor a_2 (C, nor_6_out, X);
  nor nor_7 (nor_7_out, W, X, Y);
  nor nor_8 (nor_8_out, Y, Y);
  nor nor_9 (nor_9_out, nor_8_out, W);
  nor nor_10 (G, W, X, Y);
  nor u_d (D, nor_7_out, nor_7_out);
  nor a_3 (B, nor_9_out, X);

  assign e_2 = E;
  assign f_2 = F;
endmodule
