// Logisim project SOP(L).circ as structural Verilog: 1 circuit, main circuit main
module main (
  input  A,
  input  B,
  input  C,
  input  D,
  input  E,
  input  F,
  input  G,
  input  W,
  input  X,
  input  Y,
  input  in_11,
  input  in_12
);

  wire and_1_out, and_2_out, and_3_out, and_4_out, and_5_out, and_6_out, and_7_out, not_1_out, not_2_out,
       not_3_out;

  not not_1 (not_1_out, W);
  not not_2 (not_2_out, X);
  not not_3 (not_3_out, Y);
  and and_1 (and_1_out, not_2_out, not_3_out);
  and and_2 (and_2_out, W, not_2_out);
  and and_3 (and_3_out, X, Y);
  and and_4 (and_4_out, not_2_out, not_3_out);
  and and_5 (and_5_out, W, Y);
  or or_1 (A, and_1_out, and_2_out, and_3_out);
  or or_2 (C, and_4_out, and_5_out);
  _7_Segment_Display #(.active("false")) u_7_segment_display_1 (
    .g(G), .f(F), .a(A), .b(B), .e(E), .d(D), .c(C));  // open: dp
  and and_6 (and_6_out, not_2_out, not_3_out);
  and and_7 (and_7_out, W, Y);
  or or_3 (D, W, X, Y);
  or or_4 (B, and_6_out, and_7_out);
  and and_8 (G, not_1_out, not_2_out, not_3_out);

  assign in_11 = F;
  assign in_12 = E;
endmodule
