// Logisim project SOP(NAND)(L).circ as structural Verilog: 1 circuit, main circuit main
module main (
  input  A,
  input  B,
  input  C,
  input  D,
  input  E,
  input  F,
  input  G,
  input  W,
  input  X,
  input  Y,
  input  f_2,
  input  e_2
);

  wire nand_1_out, nand_2_out, nand_3_out, nand_4_out, nand_5_out, nand_6_out, nand_7_out, nand_8_out,
       nand_10_out, nand_11_out, nand_12_out, nand_13_out, nand_14_out, nand_15_out, nand_16_out,
       nand_17_out, nand_18_out, nand_19_out, nand_20_out, nand_21_out;

  nand nand_1 (nand_1_out, X, X);
  nand nand_2 (nand_2_out, X, X);
  nand nand_3 (nand_3_out, Y, Y);
  nand nand_4 (nand_4_out, X, X);
  nand nand_5 (nand_5_out, Y, Y);
  nand nand_6 (nand_6_out, nand_2_out, nand_3_out);
  nand nand_7 (nand_7_out, W, Y);
  nand nand_8 (nand_8_out, X, Y);
  // NAND_Gate nand_9 has open pins: in0=nand_1_out, in1=W, out=open
  nand nand_10 (nand_10_out, nand_4_out, nand_5_out);
  nand u_a (A, nand_8_out, nand_10_out);
  nand u_c (C, nand_6_out, nand_7_out);
  _7_Segment_Display #(.active("false")) u_7_segment_display_1 (
    .g(G), .f(F), .a(A), .b(B), .e(E), .d(D), .c(C));  // open: dp
  nand nand_11 (nand_11_out, W, W);
  nand nand_12 (nand_12_out, X, X);
  nand nand_13 (nand_13_out, Y, Y);
  nand nand_14 (nand_14_out, X, X);
  nand nand_15 (nand_15_out, Y, Y);
  nand nand_16 (nand_16_out, W, W);
  nand nand_17 (nand_17_out, X, X);
  nand nand_18 (nand_18_out, Y, Y);
  nand nand_19 (nand_19_out, nand_14_out, nand_15_out);
  nand nand_20 (nand_20_out, W, Y);
  nand nand_21 (nand_21_out, nand_16_out, nand_17_out, nand_18_out);
  nand u_b (D, nand_11_out, nand_12_out, nand_13_out);
  nand u_d (B, nand_19_out, nand_20_out);
  nand u_g (G, nand_21_out, nand_21_out);

  assign e_2 = E;
  assign f_2 = F;
endmodule
