// Logisim project SOP(NAND-NOT)(O).circ as structural Verilog: 1 circuit, main circuit main
module main (
  input  A,
  input  B,
  input  C,
  input  D,
  input  E,
  input  F,
  input  G,
  input  W,
  input  X,
  input  Y,
  input  f_2,
  input  e_2
);

  wire nand_1_out, nand_2_out, nand_3_out, nand_4_out, nand_5_out, nand_6_out, nand_7_out, nand_8_out,
       not_1_out, not_2_out;

  not not_1 (not_1_out, W);
  not not_2 (not_2_out, X);
  not not_3 (not_2_out, Y);
  nand nand_1 (nand_1_out, not_2_out, not_2_out);
  nand nand_2 (nand_2_out, W, not_2_out);
  nand nand_3 (nand_3_out, X, Y);
  nand nand_4 (nand_4_out, not_2_out, not_2_out);
  nand nand_5 (nand_5_out, W, Y);
  _7_Segment_Display #(.active("false")) u_7_segment_display_1 (
    .g(G), .f(F), .a(A), .b(B), .e(E), .d(D), .c(C));  // open: dp
  nand u_a (A, nand_1_out, nand_2_out, nand_3_out);
  nand u_c (C, nand_4_out, nand_5_out);
  nand nand_6 (nand_6_out, not_2_out, not_2_out);
  nand nand_7 (nand_7_out, W, Y);
  nand nand_8 (nand_8_out, not_1_out, not_2_out, not_2_out);
  nand u_d (D, not_1_out, not_2_out, not_2_out);
  nand u_b (B, nand_6_out, nand_7_out);
  nand u_g (G, nand_8_out, nand_8_out);

  assign e_2 = E;
  assign f_2 = F;
endmodule
