// Logisim project SOP(O).circ as structural Verilog: 1 circuit, main circuit main
module main (
  input  A,
  input  B,
  input  C,
  input  D,
  input  E,
  input  F,
  input  G,
  input  W,
  input  X,
  input  Y,
  input  in_11,
  input  in_12
);

  wire nand_1_out, nand_2_out, nand_3_out, nand_4_out, nand_5_out, nand_8_out, nand_9_out, nand_10_out,
       not_1_out, not_2_out, not_3_out;

  not not_1 (not_1_out, W);
  not not_2 (not_2_out, X);
  not not_3 (not_3_out, Y);
  nand nand_1 (nand_1_out, not_2_out, not_3_out);
  nand nand_2 (nand_2_out, W, not_2_out);
  nand nand_3 (nand_3_out, X, Y);
  nand nand_4 (nand_4_out, not_2_out, not_3_out);
  nand nand_5 (nand_5_out, W, Y);
  _7_Segment_Display #(.active("false")) u_7_segment_display_1 (
    .g(G), .f(F), .a(A), .b(B), .e(E), .d(D), .c(C));  // open: dp
  nand nand_6 (A, nand_1_out, nand_2_out, nand_3_out);
  nand nand_7 (C, nand_4_out, nand_5_out);
  nand nand_8 (nand_8_out, not_2_out, not_3_out);
  nand nand_9 (nand_9_out, W, Y);
  nand nand_10 (nand_10_out, W, X, Y);
  nand nand_11 (D, not_1_out, not_2_out, not_3_out);
  nand nand_12 (B, nand_8_out, nand_9_out);
  nand nand_13 (G, nand_10_out, not_3_out);

  assign in_11 = F;
  assign in_12 = E;
endmodule
