// Logisim project finalSequential.circ as structural Verilog: 1 circuit, main circuit main
module main (
  input  in_1,
  output out_2,
  output out_3,
  output out_4
);

  wire and_1_out, clock_1_out, n7408_1_pin3, n7408_1_pin6, n7408_1_pin8, n7408_1_pin11, n7408_2_pin3,
       n7408_2_pin6, n7408_2_pin12, n74138_1_pin1, n74138_1_pin2, n74138_1_pin3, n74138_1_pin4,
       n74138_1_pin6, n74138_1_pin9, n74138_1_pin10, n74138_1_pin11, n74138_1_pin12, n74138_1_pin13,
       n74138_1_pin14, n74138_1_pin15;

  _74138 #(.ShowInternalStructure("true")) u_74138_1 (
    .pin1(n74138_1_pin1), .pin2(n74138_1_pin2), .pin3(n74138_1_pin3), .pin4(n74138_1_pin4),
    .pin5(n74138_1_pin4), .pin6(n74138_1_pin6), .pin15(n74138_1_pin15), .pin14(n74138_1_pin14),
    .pin13(n74138_1_pin13), .pin12(n74138_1_pin12), .pin11(n74138_1_pin11), .pin10(n74138_1_pin10),
    .pin9(n74138_1_pin9));  // open: pin7
  Clock clock_1 (.out(clock_1_out));
  _7408 #(.ShowInternalStructure("true")) u_7408_1 (
    .pin1(n74138_1_pin11), .pin2(n74138_1_pin10), .pin3(n7408_1_pin3), .pin4(n7408_1_pin3),
    .pin5(n74138_1_pin15), .pin6(n7408_1_pin6), .pin13(n7408_1_pin3), .pin12(n74138_1_pin12),
    .pin11(n7408_1_pin11), .pin10(n74138_1_pin12), .pin9(n7408_1_pin6), .pin8(n7408_1_pin8));
  J_K_Flip_Flop j_k_ff_1 (.J(and_1_out), .K(and_1_out), .clk(clock_1_out), .Q(out_2));  // open: Qn, preset, reset
  J_K_Flip_Flop j_k_ff_2 (.J(out_4), .K(out_4), .clk(clock_1_out), .Q(out_3));  // open: Qn, preset, reset
  J_K_Flip_Flop j_k_ff_3 (.J(in_1), .K(in_1), .clk(clock_1_out), .Q(out_4));  // open: Qn, preset, reset
  _7408 #(.ShowInternalStructure("true")) u_7408_2 (
    .pin1(n7408_1_pin11), .pin2(n74138_1_pin13), .pin3(n7408_2_pin3), .pin4(n7408_2_pin3),
    .pin5(n74138_1_pin14), .pin6(n7408_2_pin6), .pin13(n74138_1_pin15), .pin12(n7408_2_pin12),
    .pin11(n7408_1_pin8), .pin10(n74138_1_pin9), .pin9(n7408_2_pin6), .pin8(n7408_2_pin12));
  and and_1 (and_1_out, out_3, out_4);
  _7_Segment_Display #(.active("false")) u_7_segment_display_1 (
    .g(n74138_1_pin15), .f(n7408_1_pin8), .a(n7408_1_pin8), .b(n7408_1_pin6), .e(n7408_1_pin8),
    .d(n7408_2_pin12), .c(n7408_1_pin6));  // open: dp
  // also tied to GND on the sheet: n74138_1_pin4
  // also tied to VCC on the sheet: n74138_1_pin6

  // Notes on the sheet:
  //   4
  //   5
  //   0
  //   3
  //   3
  //   2
  //   1
  //   b,c
  //   0
  //   a
  //   6
  //   g
  //   a
  //   f
  //   e
  //   d
  //   0
  //   1
  //   2
  //   3
  //   4
  //   5
  //   6
  //   b
  //   c
endmodule
