// Logisim project muxProject.circ as structural Verilog: 1 circuit, main circuit main
module main (
  input  y,
  input  in_2,
  input  in_3,
  input  [1:0] wx
);

  wire multiplexer_1_out, multiplexer_2_out, multiplexer_3_out, multiplexer_4_out, multiplexer_5_out,
       multiplexer_6_out, multiplexer_7_out, not_1_out;

  not not_1 (not_1_out, y);
  Multiplexer #(.select(2)) multiplexer_1 (
    .in0(not_1_out), .in1(y), .in2(in_3), .in3(not_1_out), .out(multiplexer_1_out), .sel(wx));
  Multiplexer #(.select(2)) multiplexer_2 (
    .in0(not_1_out), .in1(in_2), .in2(in_3), .in3(in_2), .out(multiplexer_2_out), .sel(wx));
  Multiplexer #(.select(2)) multiplexer_3 (
    .in0(not_1_out), .in1(in_2), .in2(in_3), .in3(in_2), .out(multiplexer_3_out), .sel(wx));
  Multiplexer #(.select(2)) multiplexer_4 (
    .in0(y), .in1(in_3), .in2(in_3), .in3(in_3), .out(multiplexer_4_out), .sel(wx));
  Multiplexer #(.select(2)) multiplexer_5 (
    .in0(in_3), .in1(in_3), .in2(in_3), .in3(in_3), .out(multiplexer_5_out), .sel(wx));
  Multiplexer #(.select(2)) multiplexer_6 (
    .in0(in_3), .in1(in_3), .in2(in_3), .in3(in_3), .out(multiplexer_6_out), .sel(wx));
  Multiplexer #(.select(2)) multiplexer_7 (
    .in0(not_1_out), .in1(in_2), .in2(in_2), .in3(in_2), .out(multiplexer_7_out), .sel(wx));
  _7_Segment_Display u_7_segment_display_1 (
    .g(multiplexer_7_out), .f(multiplexer_6_out), .a(multiplexer_1_out), .b(multiplexer_2_out),
    .e(multiplexer_5_out), .d(multiplexer_4_out), .c(multiplexer_3_out));  // open: dp
endmodule
