// Logisim project onlyWithDecoder.circ as structural Verilog: 1 circuit, main circuit main
module main (
  input  in_1,
  output out_2,
  output out_3,
  output out_4
);

  wire and_1_out, clock_1_out, decoder_1_out0, decoder_1_out1, decoder_1_out2, decoder_1_out3,
       decoder_1_out4, decoder_1_out5, decoder_1_out6, or_1_out, or_2_out, or_3_out, or_4_out;

  Decoder #(.enable("false"), .select(3)) decoder_1 (
    .out0(decoder_1_out0), .out1(decoder_1_out1), .out2(decoder_1_out2), .out3(decoder_1_out3),
    .out4(decoder_1_out4), .out5(decoder_1_out5), .out6(decoder_1_out6), .sel({out_2, out_3, out_4}));  // open: out7
  Clock clock_1 (.out(clock_1_out));
  or or_1 (or_1_out, decoder_1_out5, decoder_1_out4, decoder_1_out0);
  or or_2 (or_2_out, decoder_1_out3, or_1_out);
  or or_3 (or_3_out, decoder_1_out6, decoder_1_out5, decoder_1_out4, decoder_1_out3, decoder_1_out2, decoder_1_out1);
  J_K_Flip_Flop j_k_ff_1 (.J(and_1_out), .K(and_1_out), .clk(clock_1_out), .Q(out_2));  // open: Qn, preset, reset
  J_K_Flip_Flop j_k_ff_2 (.J(out_4), .K(out_4), .clk(clock_1_out), .Q(out_3));  // open: Qn, preset, reset
  J_K_Flip_Flop j_k_ff_3 (.J(in_1), .K(in_1), .clk(clock_1_out), .Q(out_4));  // open: Qn, preset, reset
  or or_4 (or_4_out, decoder_1_out0, or_3_out);
  and and_1 (and_1_out, out_3, out_4);
  _7_Segment_Display u_7_segment_display_1 (
    .g(decoder_1_out0), .f(or_4_out), .a(or_2_out), .b(or_1_out), .e(or_4_out), .d(or_3_out), .c(or_1_out));  // open: dp
endmodule
