// Logisim project task02.circ as structural Verilog: 1 circuit, main circuit main
module main (
  input  A,
  input  B,
  input  C,
  input  D,
  input  E,
  input  F,
  input  G,
  input  W,
  input  X,
  input  Y
);

  wire and_1_out, and_2_out, and_3_out, and_4_out, and_5_out, and_6_out, and_7_out, and_8_out, and_9_out,
       and_10_out, and_11_out, and_12_out, and_13_out, and_14_out, and_15_out, and_16_out, and_17_out,
       and_18_out, and_19_out, and_20_out, and_21_out, and_22_out, and_23_out, and_24_out, and_25_out,
       and_26_out, and_27_out, and_28_out, and_29_out, and_30_out, and_31_out, and_32_out, and_33_out,
       not_1_out, not_2_out, not_3_out;

  not not_1 (not_1_out, W);
  not not_2 (not_2_out, X);
  not not_3 (not_3_out, Y);
  and and_1 (and_1_out, not_1_out, not_2_out, not_3_out);
  and and_2 (and_2_out, not_1_out, not_2_out, Y);
  and and_3 (and_3_out, not_1_out, X, not_3_out);
  and and_4 (and_4_out, not_1_out, X, Y);
  and and_5 (and_5_out, W, not_2_out, not_3_out);
  and and_6 (and_6_out, W, X, Y);
  and and_7 (and_7_out, not_1_out, not_2_out, Y);
  and and_8 (and_8_out, W, not_2_out, not_3_out);
  and and_9 (and_9_out, W, not_2_out, Y);
  and and_10 (and_10_out, W, X, not_3_out);
  and and_11 (and_11_out, W, X, Y);
  and and_12 (and_12_out, not_1_out, not_2_out, not_3_out);
  and and_13 (and_13_out, not_1_out, X, not_3_out);
  and and_14 (and_14_out, not_1_out, X, Y);
  or or_1 (A, and_1_out, and_2_out, and_3_out, and_4_out, and_5_out, and_6_out);
  or or_2 (C, and_7_out, and_8_out, and_9_out, and_10_out, and_11_out);
  or or_3 (E, and_12_out, and_13_out, and_14_out);
  _7_Segment_Display #(.active("false")) u_7_segment_display_1 (
    .g(G), .f(F), .a(A), .b(B), .e(E), .d(D), .c(C));  // open: dp
  and and_15 (and_15_out, not_1_out, not_2_out, not_3_out);
  and and_16 (and_16_out, not_1_out, not_2_out, Y);
  and and_17 (and_17_out, not_1_out, X, not_3_out);
  and and_18 (and_18_out, not_1_out, X, Y);
  and and_19 (and_19_out, W, not_2_out, not_3_out);
  and and_20 (and_20_out, W, X, Y);
  and and_21 (and_21_out, not_1_out, X, Y);
  and and_22 (and_22_out, W, not_2_out, not_3_out);
  and and_23 (and_23_out, W, not_2_out, Y);
  and and_24 (and_24_out, W, X, not_3_out);
  and and_25 (and_25_out, W, X, Y);
  and and_26 (and_26_out, not_1_out, not_2_out, not_3_out);
  and and_27 (and_27_out, not_1_out, not_2_out, Y);
  and and_28 (and_28_out, not_1_out, X, not_3_out);
  and and_29 (and_29_out, not_1_out, not_2_out, Y);
  and and_30 (and_30_out, not_1_out, X, not_2_out);
  and and_31 (and_31_out, not_1_out, X, Y);
  and and_32 (and_32_out, W, not_2_out, not_3_out);
  and and_33 (and_33_out, W, X, Y);
  or or_4 (D, and_15_out, and_16_out, and_17_out, and_18_out, and_19_out, and_20_out);
  or or_5 (B, and_21_out, and_22_out, and_23_out, and_24_out, and_25_out);
  or or_6 (F, and_26_out, and_27_out, and_28_out);
  or or_7 (G, and_29_out, and_30_out, and_31_out, and_32_out, and_33_out);
endmodule
