// Logisim project task03.circ as structural Verilog: 1 circuit, main circuit main
module main (
  input  A,
  input  B,
  input  C,
  input  D,
  input  E,
  input  F,
  input  G,
  input  W,
  input  X,
  input  Y
);

  wire not_1_out, not_2_out, not_3_out, or_1_out, or_2_out, or_3_out, or_4_out, or_5_out, or_6_out, or_7_out,
       or_8_out, or_9_out, or_10_out, or_11_out, or_12_out, or_13_out, or_14_out, or_15_out, or_16_out,
       or_17_out, or_18_out, or_19_out, or_20_out, or_21_out, or_22_out, or_23_out;

  not not_1 (not_1_out, W);
  not not_2 (not_2_out, X);
  not not_3 (not_3_out, Y);
  or or_1 (or_1_out, W, not_2_out, Y);
  or or_2 (or_2_out, W, X, not_3_out);
  or or_3 (or_3_out, not_1_out, not_2_out, not_3_out);
  or or_4 (or_4_out, not_1_out, X, not_3_out);
  or or_5 (or_5_out, not_1_out, X, Y);
  or or_6 (or_6_out, not_1_out, not_2_out, Y);
  or or_7 (or_7_out, W, not_2_out, not_3_out);
  or or_8 (or_8_out, W, not_2_out, Y);
  or or_9 (or_9_out, W, X, not_3_out);
  or or_10 (or_10_out, W, X, Y);
  and and_1 (A, or_1_out, or_2_out);
  and and_2 (C, or_3_out, or_4_out, or_5_out);
  and and_3 (E, or_6_out, or_7_out, or_8_out, or_9_out, or_10_out);
  _7_Segment_Display #(.active("false")) u_7_segment_display_1 (
    .g(G), .f(F), .a(A), .b(B), .e(E), .d(D), .c(C));  // open: dp
  or or_11 (or_11_out, W, not_2_out, Y);
  or or_12 (or_12_out, W, X, not_3_out);
  or or_13 (or_13_out, not_1_out, not_2_out, not_3_out);
  or or_14 (or_14_out, not_1_out, not_2_out, Y);
  or or_15 (or_15_out, not_1_out, X, not_3_out);
  or or_16 (or_16_out, not_1_out, X, Y);
  or or_17 (or_17_out, W, not_2_out, not_3_out);
  or or_18 (or_18_out, W, not_2_out, Y);
  or or_19 (or_19_out, W, X, not_3_out);
  or or_20 (or_20_out, W, X, Y);
  or or_21 (or_21_out, not_1_out, not_2_out, not_3_out);
  or or_22 (or_22_out, W, not_2_out, Y);
  or or_23 (or_23_out, W, X, not_3_out);
  and and_4 (D, or_11_out, or_12_out);
  and and_5 (B, or_13_out, or_14_out, or_15_out);
  and and_6 (F, or_16_out, or_17_out, or_18_out, or_19_out, or_20_out);
  and and_7 (G, or_21_out, or_22_out, or_23_out);
endmodule
