// Logisim project task04.circ as structural Verilog: 1 circuit, main circuit main
module main (
  input  A,
  input  B,
  input  C,
  input  D,
  input  E,
  input  F,
  input  G,
  input  W,
  input  X,
  input  Y
);

  wire and_1_out, and_2_out, and_3_out, and_4_out, and_5_out, and_6_out, and_7_out, and_8_out, and_9_out,
       and_10_out, and_11_out, and_12_out, and_13_out, and_14_out, not_1_out, not_2_out, not_3_out;

  not not_1 (not_1_out, W);
  not not_2 (not_2_out, X);
  not not_3 (not_3_out, Y);
  and and_1 (and_1_out, not_2_out, not_3_out);
  and and_2 (and_2_out, X, Y);
  and and_3 (and_3_out, not_2_out, Y);
  and and_4 (and_4_out, not_1_out, X);
  and and_5 (and_5_out, not_1_out, not_3_out);
  or or_1 (A, and_1_out, not_1_out, and_2_out);
  or or_2 (C, W, and_3_out);
  or or_3 (E, and_4_out, and_5_out);
  _7_Segment_Display #(.active("false")) u_7_segment_display_1 (
    .g(G), .f(F), .a(A), .b(B), .e(E), .d(D), .c(C));  // open: dp
  and and_6 (and_6_out, not_2_out, not_3_out);
  and and_7 (and_7_out, X, Y);
  and and_8 (and_8_out, X, Y);
  and and_9 (and_9_out, not_1_out, not_2_out);
  and and_10 (and_10_out, not_1_out, not_3_out);
  and and_11 (and_11_out, not_1_out, Y);
  and and_12 (and_12_out, not_1_out, X);
  and and_13 (and_13_out, W, not_2_out, not_3_out);
  and and_14 (and_14_out, X, Y);
  or or_4 (D, not_1_out, and_6_out, and_7_out);
  or or_5 (B, W, and_8_out);
  or or_6 (F, and_9_out, and_10_out);
  or or_7 (G, and_11_out, and_12_out, and_13_out, and_14_out);
endmodule
