// Logisim project task05.circ as structural Verilog: 1 circuit, main circuit main
module main (
  input  A,
  input  B,
  input  C,
  input  D,
  input  E,
  input  F,
  input  G,
  input  W,
  input  X,
  input  Y
);

  wire not_1_out, not_2_out, not_3_out, or_1_out, or_2_out, or_3_out, or_4_out, or_5_out, or_6_out, or_7_out,
       or_8_out, or_9_out, or_10_out, or_11_out, or_12_out, or_13_out, or_14_out;

  not not_1 (not_1_out, W);
  not not_2 (not_2_out, X);
  not not_3 (not_3_out, Y);
  or or_1 (or_1_out, W, not_2_out, Y);
  or or_2 (or_2_out, W, X, not_3_out);
  or or_3 (or_3_out, not_1_out, not_3_out);
  or or_4 (or_4_out, not_1_out, X);
  or or_5 (or_5_out, not_2_out, Y);
  and and_1 (A, or_1_out, or_2_out);
  and and_2 (C, or_3_out, or_4_out);
  and and_3 (E, W, or_5_out);
  _7_Segment_Display #(.active("false")) u_7_segment_display_1 (
    .g(G), .f(F), .a(A), .b(B), .e(E), .d(D), .c(C));  // open: dp
  or or_6 (or_6_out, W, not_2_out, Y);
  or or_7 (or_7_out, W, X, not_3_out);
  or or_8 (or_8_out, not_1_out, not_2_out, not_3_out);
  or or_9 (or_9_out, not_1_out, not_2_out, Y);
  or or_10 (or_10_out, not_1_out, X, not_3_out);
  or or_11 (or_11_out, W, Y);
  or or_12 (or_12_out, not_1_out, not_2_out, not_3_out);
  or or_13 (or_13_out, W, not_2_out, Y);
  or or_14 (or_14_out, W, X, not_3_out);
  and and_4 (D, or_6_out, or_7_out);
  and and_5 (B, or_8_out, or_9_out, or_10_out);
  and and_6 (F, W, or_11_out);
  and and_7 (G, or_12_out, or_13_out, or_14_out);
endmodule
