// Logisim project assignment_excess3_to_BCD.circ as structural Verilog: 1 circuit, main circuit main
module main (
  input  B,
  input  C,
  input  D,
  input  in_4,
  input  in_5,
  input  in_6,
  output F,
  output out_8
);

  wire and_1_out, and_2_out, and_3_out, and_4_out, not_1_out, not_2_out, not_3_out;

  not not_1 (not_1_out, B);
  not not_2 (not_2_out, C);
  not not_3 (not_3_out, D);
  and and_1 (and_1_out, not_1_out, not_2_out);
  and and_2 (and_2_out, not_1_out, not_3_out);
  and and_3 (and_3_out, B, C, D);
  and and_4 (and_4_out, in_5, in_6);
  or or_1 (F, and_1_out, and_2_out, and_3_out);
  xnor xnor_1 (out_8, in_4, and_4_out);
endmodule
