// Logisim project 1st_Canolical_using_NAND_gates.circ as structural Verilog: 1 circuit, main circuit main
module main (
  input  W,
  input  X,
  input  Y
);

  wire nand_1_out, nand_2_out, nand_3_out, nand_4_out, nand_5_out, nand_6_out, nand_7_out, nand_8_out,
       nand_9_out, nand_10_out, nand_11_out, nand_12_out, nand_13_out, nand_14_out, nand_15_out, nand_16_out,
       nand_17_out, nand_18_out, nand_19_out, nand_20_out, nand_21_out, nand_22_out, nand_23_out,
       nand_24_out, nand_25_out, nand_26_out, nand_27_out;

  nand nand_1 (nand_1_out, W, W);
  nand nand_2 (nand_2_out, X, X);
  nand nand_3 (nand_3_out, Y, Y);
  nand nand_4 (nand_4_out, nand_1_out, nand_3_out);
  nand nand_5 (nand_5_out, W, X, nand_3_out);
  nand nand_6 (nand_6_out, nand_2_out, nand_3_out);
  nand nand_7 (nand_7_out, X, Y);
  nand nand_8 (nand_8_out, W, nand_2_out);
  nand nand_9 (nand_9_out, X, Y);
  nand nand_10 (nand_10_out, nand_2_out, Y);
  nand nand_11 (nand_11_out, W, nand_2_out);
  nand nand_12 (nand_12_out, W, Y);
  nand nand_13 (nand_13_out, nand_1_out, nand_2_out);
  nand nand_14 (nand_14_out, W, X);
  nand nand_15 (nand_15_out, X, nand_3_out);
  nand nand_16 (nand_16_out, X, Y);
  nand nand_17 (nand_17_out, nand_1_out, X);
  nand nand_18 (nand_18_out, nand_1_out, Y);
  nand nand_19 (nand_19_out, W, nand_2_out, nand_3_out);
  nand nand_20 (nand_20_out, nand_5_out, nand_5_out);
  nand nand_21 (nand_21_out, nand_8_out, nand_9_out);
  nand nand_22 (nand_22_out, nand_2_out, nand_4_out);
  nand nand_23 (nand_23_out, W, nand_6_out, nand_7_out);
  nand nand_24 (nand_24_out, nand_10_out, nand_11_out, nand_12_out);
  nand nand_25 (nand_25_out, W, nand_2_out, Y);
  nand nand_26 (nand_26_out, nand_13_out, nand_14_out, nand_15_out);
  nand nand_27 (nand_27_out, nand_16_out, nand_17_out, nand_18_out, nand_19_out);
  _7_Segment_Display u_7_segment_display_1 (
    .g(nand_27_out), .f(nand_26_out), .a(nand_23_out), .b(nand_21_out), .e(nand_22_out), .d(nand_25_out),
    .c(nand_24_out), .dp(nand_20_out));

  // Notes on the sheet:
  //   Name: Aziza Zaman Sadia
  //   ID: 2231603642
  //   Course & Section: CSE231.8
endmodule
