// Logisim project 1st_Canolical_using_basic_gates.circ as structural Verilog: 1 circuit, main circuit main
module main (
  input  W,
  input  X,
  input  Y
);

  wire and_1_out, and_2_out, and_3_out, and_4_out, and_5_out, and_6_out, and_7_out, and_8_out, and_9_out,
       and_10_out, and_11_out, and_12_out, and_13_out, and_14_out, and_15_out, and_16_out, not_1_out,
       not_2_out, not_3_out, or_1_out, or_2_out, or_3_out, or_4_out, or_5_out, or_6_out, or_7_out;

  not not_1 (not_1_out, W);
  not not_2 (not_2_out, X);
  not not_3 (not_3_out, Y);
  and and_1 (and_1_out, not_1_out, not_3_out);
  and and_2 (and_2_out, W, X, not_3_out);
  and and_3 (and_3_out, not_2_out, not_3_out);
  and and_4 (and_4_out, X, Y);
  and and_5 (and_5_out, W, not_2_out);
  and and_6 (and_6_out, X, Y);
  and and_7 (and_7_out, not_2_out, Y);
  and and_8 (and_8_out, W, not_2_out);
  and and_9 (and_9_out, W, Y);
  and and_10 (and_10_out, not_1_out, not_2_out);
  and and_11 (and_11_out, W, X);
  and and_12 (and_12_out, X, not_3_out);
  and and_13 (and_13_out, X, Y);
  and and_14 (and_14_out, not_1_out, X);
  and and_15 (and_15_out, not_1_out, Y);
  and and_16 (and_16_out, W, not_2_out, not_3_out);
  or or_1 (or_1_out, and_5_out, and_6_out);
  or or_2 (or_2_out, X, and_1_out);
  or or_3 (or_3_out, not_1_out, and_3_out, and_4_out);
  or or_4 (or_4_out, and_7_out, and_8_out, and_9_out);
  or or_5 (or_5_out, not_1_out, X, not_3_out);
  or or_6 (or_6_out, and_10_out, and_11_out, and_12_out);
  or or_7 (or_7_out, and_13_out, and_14_out, and_15_out, and_16_out);
  _7_Segment_Display u_7_segment_display_1 (
    .g(or_7_out), .f(or_6_out), .a(or_3_out), .b(or_1_out), .e(or_2_out), .d(or_5_out), .c(or_4_out),
    .dp(and_2_out));

  // Notes on the sheet:
  //   Name: Aziza Zaman Sadia
  //   ID: 2231603642
  //   Course & Section: CSE231.8
endmodule
