// Logisim project 2nd_Canolical_using_NOR_gates.circ as structural Verilog: 1 circuit, main circuit main
module main (
  input  W,
  input  X,
  input  Y
);

  wire nor_1_out, nor_2_out, nor_3_out, nor_4_out, nor_5_out, nor_6_out, nor_7_out, nor_8_out, nor_9_out,
       nor_10_out, nor_11_out, nor_12_out, nor_13_out, nor_14_out, nor_15_out, nor_16_out, nor_17_out,
       nor_18_out, nor_19_out, nor_20_out, nor_21_out, nor_22_out, nor_23_out, not_1_out, not_2_out,
       not_3_out;

  not not_1 (not_1_out, W);
  not not_2 (not_2_out, X);
  not not_3 (not_3_out, Y);
  nor nor_1 (nor_1_out, not_1_out, X, not_3_out);
  nor nor_2 (nor_2_out, not_1_out, not_2_out, Y);
  nor nor_3 (nor_3_out, W, X);
  nor nor_4 (nor_4_out, not_2_out, Y);
  nor nor_5 (nor_5_out, W, Y);
  nor nor_6 (nor_6_out, not_2_out, Y);
  nor nor_7 (nor_7_out, W, not_2_out);
  nor nor_8 (nor_8_out, not_1_out, X, not_3_out);
  nor nor_9 (nor_9_out, X, not_3_out);
  nor nor_10 (nor_10_out, not_1_out, X);
  nor nor_11 (nor_11_out, not_1_out, X);
  nor nor_12 (nor_12_out, W, not_2_out, not_3_out);
  nor nor_13 (nor_13_out, W, X, Y);
  nor nor_14 (nor_14_out, not_1_out, X, not_3_out);
  nor nor_15 (nor_15_out, not_1_out, not_2_out, Y);
  nor nor_16 (nor_16_out, nor_8_out, nor_8_out);
  nor nor_17 (nor_17_out, nor_3_out, nor_4_out);
  nor nor_18 (nor_18_out, nor_9_out, nor_10_out);
  nor nor_19 (nor_19_out, not_1_out, not_2_out, Y);
  nor nor_20 (nor_20_out, nor_1_out, nor_2_out);
  nor nor_21 (nor_21_out, nor_5_out, nor_6_out, nor_7_out);
  nor nor_22 (nor_22_out, nor_11_out, nor_12_out);
  nor nor_23 (nor_23_out, nor_13_out, nor_14_out, nor_15_out);
  _7_Segment_Display u_7_segment_display_1 (
    .g(nor_23_out), .f(nor_22_out), .a(nor_20_out), .b(nor_17_out), .e(nor_18_out), .d(nor_16_out),
    .c(nor_21_out), .dp(nor_19_out));

  // Notes on the sheet:
  //   Name: Aziza Zaman Sadia
  //   ID: 2231603642
  //   Course & Section: CSE231.8
endmodule
