// Logisim project 2nd_Canolical_using_basic_gates.circ as structural Verilog: 1 circuit, main circuit main
module main (
  input  W,
  input  X,
  input  Y
);

  wire and_1_out, and_2_out, and_3_out, and_4_out, and_5_out, and_6_out, and_7_out, not_1_out, not_2_out,
       not_3_out, or_1_out, or_2_out, or_3_out, or_4_out, or_5_out, or_6_out, or_7_out, or_8_out, or_9_out,
       or_10_out, or_11_out, or_12_out, or_13_out, or_14_out, or_15_out;

  not not_1 (not_1_out, W);
  not not_2 (not_2_out, X);
  not not_3 (not_3_out, Y);
  or or_1 (or_1_out, not_1_out, X, not_3_out);
  or or_2 (or_2_out, not_1_out, not_2_out, Y);
  or or_3 (or_3_out, W, X);
  or or_4 (or_4_out, not_2_out, Y);
  or or_5 (or_5_out, W, Y);
  or or_6 (or_6_out, not_2_out, Y);
  or or_7 (or_7_out, W, not_2_out);
  or or_8 (or_8_out, X, not_3_out);
  or or_9 (or_9_out, not_1_out, X);
  or or_10 (or_10_out, not_1_out, X);
  or or_11 (or_11_out, W, not_2_out, not_3_out);
  or or_12 (or_12_out, W, X, Y);
  or or_13 (or_13_out, not_1_out, X, not_3_out);
  or or_14 (or_14_out, not_1_out, not_2_out, Y);
  and and_1 (and_1_out, or_3_out, or_4_out);
  and and_2 (and_2_out, or_8_out, or_9_out);
  and and_3 (and_3_out, W, X, not_3_out);
  and and_4 (and_4_out, or_1_out, or_2_out);
  and and_5 (and_5_out, or_5_out, or_6_out, or_7_out);
  or or_15 (or_15_out, not_1_out, X, not_3_out);
  and and_6 (and_6_out, or_10_out, or_11_out);
  and and_7 (and_7_out, or_12_out, or_13_out, or_14_out);
  _7_Segment_Display u_7_segment_display_1 (
    .g(and_7_out), .f(and_6_out), .a(and_4_out), .b(and_1_out), .e(and_2_out), .d(or_15_out), .c(and_5_out),
    .dp(and_3_out));

  // Notes on the sheet:
  //   Name: Aziza Zaman Sadia
  //   ID: 2231603642
  //   Course & Section: CSE231.8
endmodule
