// Logisim project Asynchronous_counter_for_any_combination.circ as structural Verilog: 1 circuit, main circuit main
module main (
  output out_1,
  output out_2
);

  wire and_1_out, clock_1_out;

  Clock clock_1 (.out(clock_1_out));
  T_Flip_Flop #(.trigger("falling")) t_ff_1 (.T(1'b1), .clk(clock_1_out), .Q(out_1));  // open: Qn, reset, preset
  and and_1 (and_1_out, clock_1_out, out_1);
  T_Flip_Flop #(.trigger("falling")) t_ff_2 (.T(1'b1), .clk(and_1_out), .Q(out_2));  // open: Qn, reset, preset

  // Notes on the sheet:
  //   00-10-01-11
endmodule
