// Logisim project lab01_d2.circ as structural Verilog: 1 circuit, main circuit main
module main (
  input  A,
  input  B,
  input  C,
  output F
);

  wire and_1_out;

  and and_1 (and_1_out, A, B);
  and and_2 (F, and_1_out, C);

  // Notes on the sheet:
  //   1
  //   2
  //   3
  //   4
  //   5
  //   6
  //   F(A,B,C)=ABC
endmodule
