// Logisim project lab01_d2b.circ as structural Verilog: 1 circuit, main circuit main
module main (
  input  A,
  input  B,
  input  C,
  output F
);

  wire or_1_out;

  or or_1 (or_1_out, A, B);
  or or_2 (F, or_1_out, C);

  // Notes on the sheet:
  //   2
  //   1
  //   3
  //   4
  //   5
  //   6
  //   F(A,B,C)=A+B+C
endmodule
