// Logisim project lab01_d3.circ as structural Verilog: 1 circuit, main circuit main
module main (
  input  A,
  input  B,
  input  C,
  output F
);

  wire and_1_out, and_2_out, and_3_out, not_1_out, not_2_out, not_3_out, or_1_out;

  not not_1 (not_1_out, A);
  not not_2 (not_2_out, B);
  not not_3 (not_3_out, C);
  and and_1 (and_1_out, not_1_out, C);
  and and_2 (and_2_out, A, not_2_out);
  and and_3 (and_3_out, B, C);
  or or_1 (or_1_out, and_1_out, and_2_out);
  or or_2 (F, or_1_out, and_3_out);

  // Notes on the sheet:
  //   1
  //   3
  //   2
  //   4
  //   5
  //   9
  //   8
  //   10
  //   I1=A'C
  //   1
  //   2
  //   6
  //   I2=AB'
  //   I3=BC
  //   3
  //   4
  //   5
  //   6
  //   F=I1+I2+I3
endmodule
