// Logisim project canolicalForm01.circ as structural Verilog: 1 circuit, main circuit main
module main (
  input  in_1,
  input  in_2,
  input  in_3,
  output out_4
);

  wire and_1_out, and_2_out, and_3_out, not_1_out, not_2_out, not_3_out;

  not not_1 (not_1_out, in_1);
  not not_2 (not_2_out, in_2);
  not not_3 (not_3_out, in_3);
  and and_1 (and_1_out, not_1_out, not_2_out, in_3);
  and and_2 (and_2_out, not_1_out, in_2, not_3_out);
  and and_3 (and_3_out, in_1, in_2, not_3_out);
  or or_1 (out_4, and_1_out, and_2_out, and_3_out);

  // Notes on the sheet:
  //   A
  //   B
  //   1
  //   2
  //   C
  //   3
  //   4
  //   5
  //   6
  //   1
  //   2
  //   13
  //   3
  //   4
  //   5
  //   9
  //   10
  //   11
  //   A'B'C
  //   12
  //   A'BC'
  //   6
  //   ABC'
  //   8
  //   3
  //   4
  //   5
  //   6
  //                                                             F(A,B,C)=A'B'C+ A'BC'+ABC' 
endmodule
