// Logisim project canolicalForm02_IC.circ as structural Verilog: 1 circuit, main circuit main
module main (
  input  A,
  input  B,
  input  C,
  output out_4
);

  wire n7404_1_pin2, n7404_1_pin4, n7404_1_pin6, n7432_1_pin3, n7432_1_pin6, n7432_1_pin8, n7432_1_pin11,
       n7432_1_pin13, n7432_2_pin6;

  _7404 #(.ShowInternalStructure("true")) u_7404_1 (
    .pin1(A), .pin2(n7404_1_pin2), .pin3(B), .pin4(n7404_1_pin4), .pin5(C), .pin6(n7404_1_pin6));  // open: pin13, pin12, pin11, pin10, pin9, pin8
  _7432 #(.ShowInternalStructure("true")) u_7432_1 (
    .pin1(B), .pin2(C), .pin3(n7432_1_pin3), .pin4(n7432_1_pin3), .pin5(A), .pin6(n7432_1_pin6),
    .pin13(n7432_1_pin13), .pin12(n7404_1_pin2), .pin11(n7432_1_pin11), .pin10(n7432_1_pin3),
    .pin9(n7404_1_pin2), .pin8(n7432_1_pin8));
  _7432 #(.ShowInternalStructure("true")) u_7432_2 (
    .pin1(n7404_1_pin4), .pin2(n7404_1_pin6), .pin3(n7432_1_pin13), .pin4(n7432_1_pin13), .pin5(A),
    .pin6(n7432_2_pin6));  // open: pin13, pin12, pin11, pin10, pin9, pin8
  _7421 #(.ShowInternalStructure("true")) u_7421_1 (
    .pin1(n7432_1_pin8), .pin2(n7432_1_pin6), .pin4(n7432_1_pin11), .pin5(n7432_2_pin6), .pin6(out_4));  // open: pin3, pin13, pin12, pin11, pin10, pin9, pin8

  // Notes on the sheet:
  //   B'
  //   A'
  //   C'
  //   B+C
  //   B'+C'
  //   A+B+C
  //   A'+B'+C'
  //   A'+B+C
  //   Name: Aziza Zaman Sadia
  //   A+B'+C'
  //   F(A,B,C)=(A+B+C).(A+B'+C').(A'+B+C).(A'+B+C').(A'+B'+C')
endmodule
