// Logisim project LAB3_d1_XNOR_to_NAND.circ as structural Verilog: 1 circuit, main circuit main
module main (
  input  A,
  input  B,
  output F
);

  wire nand_1_out, nand_2_out, nand_3_out, nand_4_out;

  nand nand_1 (nand_1_out, A, A);
  nand nand_2 (nand_2_out, B, B);
  nand nand_3 (nand_3_out, nand_1_out, nand_2_out);
  nand nand_4 (nand_4_out, A, B);
  nand nand_5 (F, nand_3_out, nand_4_out);

  // Notes on the sheet:
  //   1
  //   1
  //   2
  //   9
  //   10
  //   3
  //   4
  //   A'
  //   5
  //   8
  //   B'
  //   12
  //   13
  //   6
  //   11
  //   (AB)'
  //   (A'B')'
  //   1
  //   2
  //   3
  //   F(A,B,C)=AB+A'B'
endmodule
