// Logisim project LAB3_d1_XOR_to_NAND.circ as structural Verilog: 1 circuit, main circuit main
module main (
  input  A,
  input  B,
  input  A_1,
  input  B_1,
  output F,
  output F_1
);

  wire nand_1_out, nand_2_out, nand_3_out, nand_4_out, nand_5_out, nand_7_out, nand_8_out;

  nand nand_1 (nand_1_out, A, A);
  nand nand_2 (nand_2_out, B, B);
  nand nand_3 (nand_3_out, nand_1_out, B);
  nand nand_4 (nand_4_out, nand_2_out, A);
  nand nand_5 (nand_5_out, A_1, B_1);
  nand nand_6 (F, nand_3_out, nand_4_out);
  nand nand_7 (nand_7_out, A_1, nand_5_out);
  nand nand_8 (nand_8_out, nand_5_out, B_1);
  nand nand_9 (F_1, nand_7_out, nand_8_out);

  // Notes on the sheet:
  //   1
  //   1
  //   2
  //   9
  //   10
  //   3
  //   4
  //   A'
  //   5
  //   8
  //   12
  //   B'
  //   13
  //   1
  //   2
  //   (A'B)'
  //   6
  //   (AB')'
  //   11
  //   3
  //   (AB)'
  //   1
  //   2
  //   4
  //   5
  //   9
  //   10
  //   3
  //   6
  //   (A.(AB)')'
  //   8
  //   (B.(AB)')'
  //   F(A,B,C)=A'B+AB'
  //   12
  //   13
  //   11
  //   F(A,B,C)=A'B+AB'
endmodule
