// Logisim project LAB3_d2_NOR.circ as structural Verilog: 1 circuit, main circuit main
module main (
  input  A,
  input  A_2,
  input  B_2,
  input  A_1,
  input  B_1,
  input  A_4,
  input  B_4,
  input  A_3,
  input  B_3,
  output F,
  output F_2,
  output F_1,
  output F_4,
  output out_14
);

  wire nor_2_out, nor_3_out, nor_4_out, nor_5_out, nor_6_out, nor_7_out, nor_8_out, nor_11_out, nor_12_out,
       nor_14_out;

  nor nor_1 (F, A, A);
  nor nor_2 (nor_2_out, A_3, B_3);
  nor nor_3 (nor_3_out, A_2, A_2);
  nor nor_4 (nor_4_out, B_2, B_2);
  nor nor_5 (nor_5_out, A_1, B_1);
  nor nor_6 (nor_6_out, A_4, B_4);
  nor nor_7 (nor_7_out, A_3, nor_2_out);
  nor nor_8 (nor_8_out, nor_2_out, B_3);
  nor nor_9 (F_2, nor_3_out, nor_4_out);
  nor nor_10 (F_1, nor_5_out, nor_5_out);
  nor nor_11 (nor_11_out, A_4, nor_6_out);
  nor nor_12 (nor_12_out, nor_6_out, B_4);
  nor nor_13 (out_14, nor_7_out, nor_8_out);
  nor nor_14 (nor_14_out, nor_11_out, nor_12_out);
  nor nor_15 (F_4, nor_14_out, nor_14_out);

  // Notes on the sheet:
  //   2
  //   3
  //   3
  //   2
  //   1
  //   F(A)=A'
  //   1
  //   2
  //   6
  //   5
  //   3
  //   2
  //   3
  //   2
  //   1
  //   3
  //   A'
  //   4
  //   B'
  //   1
  //   (A'B')'
  //   1
  //   (A+B)'
  //   6
  //   5
  //   (A+B)'
  //   9
  //   8
  //   9
  //   8
  //   6
  //   5
  //   6
  //   5
  //   9
  //   8
  //   10
  //   10
  //   F(A,B)=A.B
  //   4
  //   F(A,B)=A+B
  //   4
  //   (A+(A+B)')'
  //   10
  //   (B+(A+B)')'
  //   4
  //   (A+(A+B)')'
  //   12
  //   11
  //   (B+(A+B)')'
  //   12
  //   11
  //   13
  //   13
  //   2
  //   3
  //   F(A,B,C)=AB+A'B'
  //   1
  //   F(A,B,C)=A'B+AB'
endmodule
