// Logisim project Lab3_B1.circ as structural Verilog: 1 circuit, main circuit main
module main (
  input  A,
  input  B,
  output F
);

  wire nand_1_out, nand_3_out;

  nand nand_1 (nand_1_out, A, A);
  nand nand_2 (nand_1_out, A, A);
  nand nand_3 (nand_3_out, B, B);
  nand nand_4 (F, nand_1_out, nand_3_out);

  // Notes on the sheet:
  //   1
  //   2
  //   4
  //   5
  //   3
  //   A'
  //   B'
  //   6
  //   9
  //   10
  //   F(A,B)=A+B
  //   8
endmodule
