// Logisim project Lab3_B2.circ as structural Verilog: 1 circuit, main circuit main
module main (
  input  A,
  input  B,
  input  C,
  output F
);

  wire and_1_out, and_2_out, not_1_out;

  not not_1 (not_1_out, C);
  and and_1 (and_1_out, A, C);
  and and_2 (and_2_out, B, not_1_out);
  or or_1 (F, and_1_out, and_2_out);

  // Notes on the sheet:
  //   1
  //   2
  //   4
  //   5
  //   AC
  //   3
  //   6
  //   BC'
  //   1
  //   2
  //   3
  //   F(A,B)=AC+BC'
endmodule
