// Logisim project Lab3_B2_NAND_IC.circ as structural Verilog: 1 circuit, main circuit main
module main (
  input  A,
  input  B,
  input  C,
  output out_4
);

  wire n7400_1_pin3, n7400_1_pin6, n7400_1_pin12;

  _7400 #(.ShowInternalStructure("true")) u_7400_1 (
    .pin1(A), .pin2(C), .pin3(n7400_1_pin3), .pin4(C), .pin5(C), .pin6(n7400_1_pin6), .pin13(n7400_1_pin3),
    .pin12(n7400_1_pin12), .pin11(out_4), .pin10(B), .pin9(n7400_1_pin6), .pin8(n7400_1_pin12));

  // Notes on the sheet:
  //   Figure B2 Implementaion Using NAND IC
  //   Group: 01
  //   Course & Section: CSE231.8
endmodule
