// Logisim project Lab3_B2_NOR.circ as structural Verilog: 1 circuit, main circuit main
module main (
  input  A,
  input  B,
  input  C,
  output F
);

  wire nor_1_out, nor_2_out, nor_3_out;

  nor nor_1 (nor_1_out, C, C);
  nor nor_2 (nor_2_out, B, C);
  nor nor_3 (nor_3_out, A, nor_1_out);
  nor nor_4 (F, nor_2_out, nor_3_out);

  // Notes on the sheet:
  //   6
  //   5
  //   3
  //   2
  //   9
  //   C'
  //   4
  //   8
  //   (B+C)'
  //   1
  //   10
  //   (A+C')'
  //   11
  //   12
  //   13
  //   Group: 01
  //   Course&Section: CSE231.8
  //   F(A,B)=(B+C).(A+C')
endmodule
