// Logisim project Lab3_B2_NOR_IC.circ as structural Verilog: 1 circuit, main circuit main
module main (
  input  A,
  input  B,
  input  C,
  output out_4
);

  wire n7402_1_pin1, n7402_1_pin4, n7402_1_pin11;

  _7402 #(.ShowInternalStructure("true")) u_7402_1 (
    .pin1(n7402_1_pin1), .pin2(C), .pin3(C), .pin4(n7402_1_pin4), .pin5(n7402_1_pin1), .pin6(A),
    .pin13(out_4), .pin12(n7402_1_pin4), .pin11(n7402_1_pin11), .pin10(n7402_1_pin11), .pin9(B), .pin8(C));

  // Notes on the sheet:
  //   Figure B2 Implementaion Using NOR IC
  //   Group:01
  //   Course & Section: CSE231.8
endmodule
