// Logisim project Lab3_C2_B2_to_NOR.circ as structural Verilog: 1 circuit, main circuit main
module main (
  input  A,
  input  B,
  input  C,
  output F
);

  wire nor_1_out, nor_2_out, nor_3_out, nor_4_out, nor_5_out, nor_6_out;

  nor nor_1 (nor_1_out, A, A);
  nor nor_2 (nor_2_out, C, C);
  nor nor_3 (nor_3_out, B, B);
  nor nor_4 (nor_4_out, nor_1_out, nor_2_out);
  nor nor_5 (nor_5_out, nor_3_out, C);
  nor nor_6 (nor_6_out, nor_4_out, nor_5_out);
  nor nor_7 (F, nor_6_out, nor_6_out);

  // Notes on the sheet:
  //   1
  //   2
  //   4
  //   5
  //   13
  //   12
  //   A'
  //   9
  //   3
  //   C'
  //   10
  //   6
  //   11
  //   1
  //   2
  //   AC
  //   8
  //   BC'
  //   3
  //   4
  //   5
  //   9
  //   6
  //   10
  //   8
  //   F(A,B)=AC+BC'
endmodule
