// Logisim project Lab3_D3_B2_to_NAND.circ as structural Verilog: 1 circuit, main circuit main
module main (
  input  A,
  input  B,
  input  C,
  output F
);

  wire nand_1_out, nand_2_out, nand_3_out;

  nand nand_1 (nand_1_out, C, C);
  nand nand_2 (nand_2_out, A, C);
  nand nand_3 (nand_3_out, B, nand_1_out);
  nand nand_4 (F, nand_2_out, nand_3_out);

  // Notes on the sheet:
  //   1
  //   2
  //   4
  //   5
  //   C'
  //   3
  //   AC
  //   6
  //   BC'
  //   Group: 01
  //   Course & Section: CSE231.8
  //   1
  //   2
  //   3
  //   F(A,B)=AC+BC'
endmodule
