// Logisim project Lab3_d2_NAND_IC.circ as structural Verilog: 1 circuit, main circuit main
module main (
  input  A,
  input  A1,
  input  B1,
  input  A2,
  input  B2,
  input  A3,
  input  B3,
  input  A4,
  input  B4,
  output F,
  output F1,
  output F2,
  output F3,
  output F4
);

  wire n7400_2_pin3, n7400_2_pin6, n7400_3_pin3, n7400_4_pin3, n7400_4_pin6, n7400_4_pin11, n7400_4_pin13,
       n7400_5_pin3, n7400_5_pin6, n7400_5_pin13;

  _7400 #(.ShowInternalStructure("true")) u_7400_1 (
    .pin1(A), .pin2(A), .pin3(F));  // open: pin4, pin5, pin6, pin13, pin12, pin11, pin10, pin9, pin8
  _7400 #(.ShowInternalStructure("true")) u_7400_2 (
    .pin1(B1), .pin2(B1), .pin3(n7400_2_pin3), .pin4(A1), .pin5(A1), .pin6(n7400_2_pin6),
    .pin10(n7400_2_pin3), .pin9(n7400_2_pin6), .pin8(F1));  // open: pin13, pin12, pin11
  _7400 #(.ShowInternalStructure("true")) u_7400_3 (
    .pin1(A2), .pin2(B2), .pin3(n7400_3_pin3), .pin4(n7400_3_pin3), .pin5(n7400_3_pin3), .pin6(F2));  // open: pin13, pin12, pin11, pin10, pin9, pin8
  _7400 #(.ShowInternalStructure("true")) u_7400_4 (
    .pin1(A3), .pin2(B3), .pin3(n7400_4_pin3), .pin4(n7400_4_pin3), .pin5(A3), .pin6(n7400_4_pin6),
    .pin13(n7400_4_pin13), .pin12(n7400_4_pin6), .pin11(n7400_4_pin11), .pin10(B3), .pin9(n7400_4_pin3),
    .pin8(n7400_4_pin13));
  _7400 #(.ShowInternalStructure("true")) u_7400_5 (
    .pin1(A4), .pin2(B4), .pin3(n7400_5_pin3), .pin4(n7400_5_pin3), .pin5(A4), .pin6(n7400_5_pin6),
    .pin13(n7400_5_pin13), .pin12(n7400_5_pin6), .pin11(F4), .pin10(B4), .pin9(n7400_5_pin3),
    .pin8(n7400_5_pin13));
  _7400 #(.ShowInternalStructure("true")) u_7400_6 (
    .pin1(n7400_4_pin11), .pin2(n7400_4_pin11), .pin3(F3));  // open: pin4, pin5, pin6, pin13, pin12, pin11, pin10, pin9, pin8

  // Notes on the sheet:
  //   NOT Gate Implementation Using NAND IC
  //   OR Gate Implementation Using NAND IC
  //   AND Gate Implementation Using NAND IC
  //   XNOR Gate Implementation Using NAND IC
  //   XOR Gate Implementation Using NAND IC
endmodule
