// Logisim project Lab3_d2_NOR_IC.circ as structural Verilog: 1 circuit, main circuit main
module main (
  input  A,
  input  A1,
  input  B1,
  input  A2,
  input  B2,
  input  A3,
  input  B3,
  input  A4,
  input  B4,
  output F,
  output F1,
  output F2,
  output F3,
  output F4
);

  wire n7402_2_pin1, n7402_2_pin4, n7402_3_pin1, n7402_4_pin1, n7402_4_pin4, n7402_4_pin11, n7402_4_pin13,
       n7402_5_pin1, n7402_5_pin4, n7402_5_pin11;

  _7402 #(.ShowInternalStructure("true")) u_7402_1 (
    .pin1(F), .pin2(A), .pin3(A));  // open: pin4, pin5, pin6, pin13, pin12, pin11, pin10, pin9, pin8
  _7402 #(.ShowInternalStructure("true")) u_7402_2 (
    .pin1(n7402_2_pin1), .pin2(B1), .pin3(B1), .pin4(n7402_2_pin4), .pin5(A1), .pin6(A1), .pin10(F1),
    .pin9(n7402_2_pin4), .pin8(n7402_2_pin1));  // open: pin13, pin12, pin11
  _7402 #(.ShowInternalStructure("true")) u_7402_3 (
    .pin1(n7402_3_pin1), .pin2(B2), .pin3(A2), .pin4(F2), .pin5(n7402_3_pin1), .pin6(n7402_3_pin1));  // open: pin13, pin12, pin11, pin10, pin9, pin8
  _7402 #(.ShowInternalStructure("true")) u_7402_4 (
    .pin1(n7402_4_pin1), .pin2(A3), .pin3(B3), .pin4(n7402_4_pin4), .pin5(n7402_4_pin1), .pin6(A3),
    .pin13(n7402_4_pin13), .pin12(n7402_4_pin4), .pin11(n7402_4_pin11), .pin10(n7402_4_pin11),
    .pin9(n7402_4_pin1), .pin8(B3));
  _7402 #(.ShowInternalStructure("true")) u_7402_5 (
    .pin1(n7402_5_pin1), .pin2(A4), .pin3(B4), .pin4(n7402_5_pin4), .pin5(n7402_5_pin1), .pin6(A4),
    .pin13(F4), .pin12(n7402_5_pin4), .pin11(n7402_5_pin11), .pin10(n7402_5_pin11), .pin9(n7402_5_pin1),
    .pin8(B4));
  _7402 #(.ShowInternalStructure("true")) u_7402_6 (
    .pin1(F3), .pin2(n7402_4_pin13), .pin3(n7402_4_pin13));  // open: pin4, pin5, pin6, pin13, pin12, pin11, pin10, pin9, pin8

  // Notes on the sheet:
  //   NOT Gate Implementation Using NOR IC
  //   AND Gate Implementation Using NOR IC
  //   OR Gate Implementation Using NOR IC
  //   XOR Gate Implementation Using NOR IC
  //   XNOR Gate Implementation Using NOR IC
endmodule
