// Logisim project Lab_07_JOB_2_MUX_IC.circ as structural Verilog: 1 circuit, main circuit main
module main (
  input  D,
  input  A,
  input  B,
  input  C,
  output out_5
);

  wire n74151_1_pin1, n74151_1_pin4, n74151_1_pin7;

  _74151 #(.ShowInternalStructure("true")) u_74151_1 (
    .pin1(n74151_1_pin1), .pin2(D), .pin3(D), .pin4(n74151_1_pin4), .pin5(out_5), .pin7(n74151_1_pin7),
    .pin15(n74151_1_pin4), .pin14(n74151_1_pin1), .pin13(n74151_1_pin1), .pin12(n74151_1_pin4), .pin11(C),
    .pin10(B), .pin9(A));  // open: pin6
  // also tied to GND on the sheet: {n74151_1_pin7, n74151_1_pin1}
  // also tied to VCC on the sheet: n74151_1_pin4

  // Notes on the sheet:
  //   ID: 2231603642
  //   Group: 01
  //   Course & Section: CSE231.8
  //   Name: Aziza Zaman Sadia
endmodule
