// Logisim project Lab_07_JOB_3_Decoder.circ as structural Verilog: 1 circuit, main circuit main
module main (
  input  C,
  input  B,
  input  A,
  output Y0,
  output Y1,
  output Y2,
  output Y3,
  output Y4,
  output Y5,
  output Y6,
  output Y7
);

  wire n74138_1_pin4, n74138_1_pin6;

  _74138 #(.ShowInternalStructure("true")) u_74138_1 (
    .pin1(A), .pin2(B), .pin3(C), .pin4(n74138_1_pin4), .pin5(n74138_1_pin4), .pin6(n74138_1_pin6),
    .pin7(Y7), .pin15(Y0), .pin14(Y1), .pin13(Y2), .pin12(Y3), .pin11(Y4), .pin10(Y5), .pin9(Y6));
  // also tied to GND on the sheet: n74138_1_pin4
  // also tied to VCC on the sheet: n74138_1_pin6

  // Notes on the sheet:
  //   Group:01
  //   Course & Section: CSE231.8
  //   Name: Aziza Zaman Sadia
  //   ID: 2231603642
endmodule
