// Logisim project D_Flip_FLop.circ as structural Verilog: 1 circuit, main circuit main
module main (
  input  x,
  output A,
  output B,
  output Y
);

  wire and_1_out, clock_1_out, d_ff_1_qn, not_1_out, xor_1_out;

  Clock clock_1 (.out(clock_1_out));
  not not_1 (not_1_out, x);
  D_Flip_Flop d_ff_1 (.D(xor_1_out), .clk(clock_1_out), .Q(A), .Qn(d_ff_1_qn));  // open: preset, reset
  xor xor_1 (xor_1_out, A, x);
  D_Flip_Flop d_ff_2 (.D(and_1_out), .clk(clock_1_out), .Q(B));  // open: Qn, preset, reset
  and and_1 (and_1_out, d_ff_1_qn, not_1_out);
  and and_2 (Y, d_ff_1_qn, x);

  // Notes on the sheet:
  //   Group: 01
  //   ID: 2231603642
  //   Course & Section: CSE231.8L
  //   Name: Aziza Zaman Sadia
endmodule
