// Logisim project JK_Flip_FLop.circ as structural Verilog: 1 circuit, main circuit main
module main (
  input  x,
  output A,
  output B,
  output Y
);

  wire and_1_out, clock_1_out, j_k_ff_1_qn, not_1_out;

  Clock clock_1 (.out(clock_1_out));
  not not_1 (not_1_out, x);
  J_K_Flip_Flop j_k_ff_1 (.J(x), .K(x), .clk(clock_1_out), .Q(A), .Qn(j_k_ff_1_qn));  // open: preset, reset
  J_K_Flip_Flop j_k_ff_2 (.J(and_1_out), .K(x), .clk(clock_1_out), .Q(B));  // open: Qn, preset, reset
  and and_1 (and_1_out, j_k_ff_1_qn, not_1_out);
  and and_2 (Y, j_k_ff_1_qn, x);

  // Notes on the sheet:
  //   Group: 01
  //   ID: 2231603642
  //   Course & Section: CSE231.8L
  //   Name: Aziza Zaman Sadia
endmodule
