// Logisim project T_Flip_FLop.circ as structural Verilog: 1 circuit, main circuit main
module main (
  input  x,
  output A,
  output B,
  output Y
);

  wire and_1_out, and_2_out, clock_1_out, not_1_out, or_1_out, t_ff_1_qn, t_ff_2_qn;

  Clock clock_1 (.out(clock_1_out));
  not not_1 (not_1_out, x);
  and and_1 (and_1_out, t_ff_1_qn, not_1_out, t_ff_2_qn);
  and and_2 (and_2_out, x, B);
  T_Flip_Flop t_ff_1 (.T(x), .clk(clock_1_out), .Q(A), .Qn(t_ff_1_qn));  // open: reset, preset
  T_Flip_Flop t_ff_2 (.T(or_1_out), .clk(clock_1_out), .Q(B), .Qn(t_ff_2_qn));  // open: reset, preset
  or or_1 (or_1_out, and_1_out, and_2_out);
  and and_3 (Y, t_ff_1_qn, x);

  // Notes on the sheet:
  //   Group: 01
  //   ID: 2231603642
  //   Course & Section: CSE231.8L
  //   Name: Aziza Zaman Sadia
endmodule
