// Logisim project Mod_6_ripple_Up_down.circ as structural Verilog: 1 circuit, main circuit main
module main (
  input  in_1,
  output out_2,
  output out_3,
  output out_4
);

  wire and_1_out, clock_1_out, multiplexer_1_out, multiplexer_2_out, not_1_out, t_ff_2_qn, t_ff_3_qn,
       undriven, undriven_2, undriven_3;

  and and_1 (and_1_out, out_3, undriven, not_1_out);
  not not_1 (not_1_out, undriven_2);
  Demultiplexer demultiplexer_1 ();  // open: out0, out1, in, sel
  T_Flip_Flop #(.trigger("falling")) t_ff_1 (.T(1'b1), .clk(multiplexer_1_out), .Q(out_2));  // open: Qn, reset, preset
  Multiplexer multiplexer_1 (.in0(out_3), .in1(t_ff_2_qn), .out(multiplexer_1_out), .sel(in_1));
  T_Flip_Flop #(.trigger("falling")) t_ff_2 (
    .T(1'b1), .clk(multiplexer_2_out), .Q(out_3), .Qn(t_ff_2_qn), .reset(undriven_3));  // open: preset
  Multiplexer multiplexer_2 (.in0(out_4), .in1(t_ff_3_qn), .out(multiplexer_2_out), .sel(in_1));
  T_Flip_Flop #(.trigger("falling")) t_ff_3 (
    .T(1'b1), .clk(clock_1_out), .Q(out_4), .Qn(t_ff_3_qn));  // open: reset, preset
  Clock clock_1 (.out(clock_1_out));
endmodule
