// Logisim project simulation_1_with_ICs_for_ease.circ as structural Verilog: 1 circuit, main circuit main
module main (
);

  wire dipswitch_1_p1, dipswitch_1_p2, dipswitch_1_p3, dipswitch_1_p4, n7404_1_pin2, n7404_1_pin4,
       n7404_1_pin6, n7404_1_pin8, n7408_1_pin3, n7408_1_pin6, n7408_1_pin8, n7486_1_pin2, n7486_1_pin3,
       n7486_1_pin5, n7486_1_pin6, n7486_1_pin8, n7486_1_pin10, n7486_1_pin11, n7486_1_pin13, n74157_1_pin2,
       n74157_1_pin3, n74157_1_pin4, n74157_1_pin5, n74157_1_pin6, n74157_1_pin7, n74157_1_pin15;

  // DipSwitch #(.number(4)) dipswitch_1: pin names not known; wires that end beside it: dipswitch_1_p1, dipswitch_1_p2, dipswitch_1_p3, dipswitch_1_p4
  _7486 #(.ShowInternalStructure("true")) u_7486_1 (
    .pin1(dipswitch_1_p1), .pin2(n7486_1_pin2), .pin3(n7486_1_pin3), .pin4(dipswitch_1_p2),
    .pin5(n7486_1_pin5), .pin6(n7486_1_pin6), .pin13(n7486_1_pin13), .pin12(dipswitch_1_p4),
    .pin11(n7486_1_pin11), .pin10(n7486_1_pin10), .pin9(dipswitch_1_p3), .pin8(n7486_1_pin8));
  _7404 #(.ShowInternalStructure("true")) u_7404_1 (
    .pin1(n7486_1_pin3), .pin2(n7404_1_pin2), .pin3(n7486_1_pin6), .pin4(n7404_1_pin4), .pin5(n7486_1_pin8),
    .pin6(n7404_1_pin6), .pin9(n7486_1_pin11), .pin8(n7404_1_pin8));  // open: pin13, pin12, pin11, pin10
  // DipSwitch #(.number(4)) dipswitch_2: pin names not known; wires that end beside it: n7486_1_pin2, n7486_1_pin5, n7486_1_pin10, n7486_1_pin13
  _7408 #(.ShowInternalStructure("true")) u_7408_1 (
    .pin1(n7404_1_pin2), .pin2(n7404_1_pin4), .pin3(n7408_1_pin3), .pin4(n7408_1_pin3), .pin5(n7404_1_pin6),
    .pin6(n7408_1_pin6), .pin10(n7404_1_pin8), .pin9(n7408_1_pin6), .pin8(n7408_1_pin8));  // open: pin13, pin12, pin11
  _7_Segment_Display u_7_segment_display_1 (
    .g(1'b1), .f(1'b0), .a(1'b0), .b(1'b0), .e(1'b1), .d(n74157_1_pin7), .c(1'b1));  // open: dp
  _74157 #(.ShowInternalStructure("true")) u_74157_1 (
    .pin1(n7408_1_pin8), .pin2(n74157_1_pin2), .pin3(n74157_1_pin3), .pin4(n74157_1_pin4),
    .pin5(n74157_1_pin5), .pin6(n74157_1_pin6), .pin7(n74157_1_pin7), .pin15(n74157_1_pin15));  // open: pin14, pin13, pin12, pin11, pin10, pin9
  LED led_1 (.in(n7408_1_pin8));
  _7_Segment_Display u_7_segment_display_2 (
    .g(1'b1), .f(1'b0), .a(1'b0), .b(1'b0), .e(1'b1), .d(n74157_1_pin4), .c(1'b1));  // open: dp
  // also tied to GND on the sheet: {n74157_1_pin3, n74157_1_pin5, n74157_1_pin15}
  // also tied to VCC on the sheet: {n74157_1_pin2, n74157_1_pin6}

  // Notes on the sheet:
  //   Admin (Set Password Here)
  //   User
endmodule
