// Logisim project simulation_1_with_flip_flops.circ as structural Verilog: 1 circuit, main circuit main
module main (
  output out_1,
  output out_2,
  output out_3,
  output out_4,
  output out_5,
  output out_6,
  output out_7,
  output out_8,
  output out_9
);

  wire and_1_out, clock_1_out, d_ff_2_q, d_ff_3_q, d_ff_4_q, dipswitch_2_p1, dipswitch_2_p2, dipswitch_2_p3,
       dipswitch_2_p4, multiplexer_1_out, multiplexer_2_out, n7404_1_pin2, n7404_1_pin4, n7404_1_pin6,
       n7404_1_pin8, n7408_1_pin3, n7408_1_pin6, n7408_1_pin8, n7486_1_pin2, n7486_1_pin3, n7486_1_pin5,
       n7486_1_pin6, n7486_1_pin8, n7486_1_pin10, n7486_1_pin11, n7486_1_pin13, n74157_1_pin2, n74157_1_pin3,
       n74157_1_pin4, n74157_1_pin5, n74157_1_pin6, n74157_1_pin7, n74157_1_pin15, not_1_out, not_2_out,
       not_3_out, not_4_out, not_5_out, undriven, xor_1_out, xor_2_out, xor_3_out, xor_4_out;

  Clock clock_1 (.out(clock_1_out));
  D_Flip_Flop d_ff_1 (.D(undriven), .clk(clock_1_out), .Q(out_9), .reset(not_1_out));  // open: Qn, preset
  D_Flip_Flop d_ff_2 (.D(d_ff_2_q), .clk(clock_1_out), .Q(d_ff_2_q), .reset(not_1_out));  // open: Qn, preset
  D_Flip_Flop d_ff_3 (.D(d_ff_3_q), .clk(clock_1_out), .Q(d_ff_3_q), .reset(not_1_out));  // open: Qn, preset
  D_Flip_Flop d_ff_4 (.D(d_ff_4_q), .clk(clock_1_out), .Q(d_ff_4_q), .reset(not_1_out));  // open: Qn, preset
  DipSwitch #(.number(4)) dipswitch_1 (.sw1(out_5), .sw2(out_6), .sw3(out_7), .sw4(out_8));
  // DipSwitch #(.number(4)) dipswitch_2: pin names not known; wires that end beside it: dipswitch_2_p1, dipswitch_2_p2, dipswitch_2_p3, dipswitch_2_p4
  _7486 #(.ShowInternalStructure("true")) u_7486_1 (
    .pin1(dipswitch_2_p1), .pin2(n7486_1_pin2), .pin3(n7486_1_pin3), .pin4(dipswitch_2_p2),
    .pin5(n7486_1_pin5), .pin6(n7486_1_pin6), .pin13(n7486_1_pin13), .pin12(dipswitch_2_p4),
    .pin11(n7486_1_pin11), .pin10(n7486_1_pin10), .pin9(dipswitch_2_p3), .pin8(n7486_1_pin8));
  // NOT_Gate not_1 has open pins: in=open, out=not_1_out
  xor xor_1 (xor_1_out, out_5, out_1);
  xor xor_2 (xor_2_out, out_6, out_2);
  xor xor_3 (xor_3_out, out_7, out_3);
  xor xor_4 (xor_4_out, out_8, out_4);
  _7404 #(.ShowInternalStructure("true")) u_7404_1 (
    .pin1(n7486_1_pin3), .pin2(n7404_1_pin2), .pin3(n7486_1_pin6), .pin4(n7404_1_pin4), .pin5(n7486_1_pin8),
    .pin6(n7404_1_pin6), .pin9(n7486_1_pin11), .pin8(n7404_1_pin8));  // open: pin13, pin12, pin11, pin10
  not not_2 (not_2_out, xor_1_out);
  not not_3 (not_3_out, xor_2_out);
  not not_4 (not_4_out, xor_3_out);
  not not_5 (not_5_out, xor_4_out);
  // DipSwitch #(.number(4)) dipswitch_3: pin names not known; wires that end beside it: n7486_1_pin2, n7486_1_pin5, n7486_1_pin10, n7486_1_pin13
  DipSwitch #(.number(4)) dipswitch_4 (.sw1(out_1), .sw2(out_2), .sw3(out_3), .sw4(out_4));
  and and_1 (and_1_out, not_2_out, not_3_out, not_4_out, not_5_out);
  _7408 #(.ShowInternalStructure("true")) u_7408_1 (
    .pin1(n7404_1_pin2), .pin2(n7404_1_pin4), .pin3(n7408_1_pin3), .pin4(n7408_1_pin3), .pin5(n7404_1_pin6),
    .pin6(n7408_1_pin6), .pin10(n7404_1_pin8), .pin9(n7408_1_pin6), .pin8(n7408_1_pin8));  // open: pin13, pin12, pin11
  Multiplexer multiplexer_1 (.in0(1'b1), .in1(1'b0), .out(multiplexer_1_out), .sel(and_1_out));
  _7_Segment_Display u_7_segment_display_1 (
    .g(multiplexer_1_out), .f(multiplexer_2_out), .a(multiplexer_2_out), .b(multiplexer_2_out), .e(1'b1),
    .d(multiplexer_2_out), .c(1'b1));  // open: dp
  _7_Segment_Display u_7_segment_display_2 (
    .g(1'b1), .f(1'b0), .a(1'b0), .b(1'b0), .e(1'b1), .d(n74157_1_pin7), .c(1'b1));  // open: dp
  _74157 #(.ShowInternalStructure("true")) u_74157_1 (
    .pin1(n7408_1_pin8), .pin2(n74157_1_pin2), .pin3(n74157_1_pin3), .pin4(n74157_1_pin4),
    .pin5(n74157_1_pin5), .pin6(n74157_1_pin6), .pin7(n74157_1_pin7), .pin15(n74157_1_pin15));  // open: pin14, pin13, pin12, pin11, pin10, pin9
  _7_Segment_Display u_7_segment_display_3 (
    .g(multiplexer_2_out), .f(multiplexer_1_out), .a(multiplexer_1_out), .b(multiplexer_1_out), .e(1'b1),
    .d(multiplexer_1_out), .c(1'b1));  // open: dp
  LED led_1 (.in(n7408_1_pin8));
  _7_Segment_Display u_7_segment_display_4 (
    .g(1'b1), .f(1'b0), .a(1'b0), .b(1'b0), .e(1'b1), .d(n74157_1_pin4), .c(1'b1));  // open: dp
  Multiplexer multiplexer_2 (.in0(1'b0), .in1(1'b1), .out(multiplexer_2_out), .sel(and_1_out));
  LED led_2 (.in(and_1_out));
  // also tied to GND on the sheet: {n74157_1_pin3, n74157_1_pin5, n74157_1_pin15}
  // also tied to VCC on the sheet: {n74157_1_pin2, n74157_1_pin6}

  // Notes on the sheet:
  //   Admin (Set Password Here)
  //   User
endmodule
