// Logisim project simulation_1_without_using_complexity.circ as structural Verilog: 1 circuit, main circuit main
module main (
  output out_1,
  output out_2,
  output out_3,
  output out_4,
  output out_5,
  output out_6,
  output out_7,
  output out_8
);

  wire and_1_out, clock_1_out, d_ff_1_q, d_ff_2_q, d_ff_3_q, d_ff_4_q, d_ff_5_q, d_ff_6_q, d_ff_7_q,
       d_ff_8_q, not_1_out, not_2_out, not_3_out, not_4_out, not_5_out, undriven, xor_1_out, xor_2_out,
       xor_3_out, xor_4_out;

  Clock clock_1 (.out(clock_1_out));
  DipSwitch #(.number(4)) dipswitch_1 (.sw1(out_5), .sw2(out_6), .sw3(out_7), .sw4(out_8));
  D_Flip_Flop d_ff_1 (.D(out_5), .clk(clock_1_out), .Q(d_ff_1_q));  // open: Qn, preset, reset
  D_Flip_Flop d_ff_2 (.D(out_6), .clk(clock_1_out), .Q(d_ff_2_q));  // open: Qn, preset, reset
  D_Flip_Flop d_ff_3 (.D(out_7), .clk(clock_1_out), .Q(d_ff_3_q));  // open: Qn, preset, reset
  D_Flip_Flop d_ff_4 (.D(out_8), .clk(clock_1_out), .Q(d_ff_4_q));  // open: Qn, preset, reset
  xor xor_1 (xor_1_out, d_ff_1_q, out_1);
  xor xor_2 (xor_2_out, d_ff_2_q, out_2);
  xor xor_3 (xor_3_out, d_ff_3_q, out_3);
  xor xor_4 (xor_4_out, d_ff_4_q, out_4);
  not not_1 (not_1_out, xor_1_out);
  not not_2 (not_2_out, xor_2_out);
  not not_3 (not_3_out, xor_3_out);
  not not_4 (not_4_out, xor_4_out);
  Hex_Digit_Display hex_digit_display_1 (.value({out_4, out_3, out_2, out_1}));  // open: dp
  and and_1 (and_1_out, not_1_out, not_2_out, not_3_out, not_4_out);
  D_Flip_Flop d_ff_5 (.D(d_ff_5_q), .clk(undriven), .Q(d_ff_5_q), .reset(not_5_out));  // open: Qn, preset
  D_Flip_Flop d_ff_6 (.D(d_ff_6_q), .clk(undriven), .Q(d_ff_6_q), .reset(not_5_out));  // open: Qn, preset
  D_Flip_Flop d_ff_7 (.D(d_ff_7_q), .clk(undriven), .Q(d_ff_7_q), .reset(not_5_out));  // open: Qn, preset
  D_Flip_Flop d_ff_8 (.D(d_ff_8_q), .clk(undriven), .Q(d_ff_8_q), .reset(not_5_out));  // open: Qn, preset
  DipSwitch #(.number(4)) dipswitch_2 (.sw1(out_1), .sw2(out_2), .sw3(out_3), .sw4(out_4));
  // NOT_Gate not_5 has open pins: in=open, out=not_5_out
  LED led_1 (.in(and_1_out));
endmodule
