// Logisim project bEHALAL.circ as structural Verilog: 1 circuit, main circuit main
module main (
  input  in_1,
  input  z_prime,
  input  y_prime,
  input  in_4
);

  wire n7404_1_pin2, n7404_1_pin4, n7404_1_pin6, n7408_1_pin3, n7408_1_pin6, n7408_1_pin8, n7408_1_pin11,
       n7408_2_pin3, n7408_2_pin11, n7432_1_pin3, n7432_1_pin6, n7432_1_pin8;

  _7404 #(.ShowInternalStructure("true")) u_7404_1 (
    .pin1(y_prime), .pin2(n7404_1_pin2), .pin3(z_prime), .pin4(n7404_1_pin4), .pin5(in_1), .pin6(n7404_1_pin6));  // open: pin13, pin12, pin11, pin10, pin9, pin8
  _7408 #(.ShowInternalStructure("true")) u_7408_1 (
    .pin1(y_prime), .pin2(in_1), .pin3(n7408_1_pin3), .pin4(n7408_1_pin3), .pin5(n7404_1_pin4),
    .pin6(n7408_1_pin6), .pin13(n7404_1_pin2), .pin12(n7404_1_pin4), .pin11(n7408_1_pin11), .pin10(y_prime),
    .pin9(z_prime), .pin8(n7408_1_pin8));
  _7408 #(.ShowInternalStructure("true")) u_7408_2 (
    .pin1(n7404_1_pin2), .pin2(n7404_1_pin6), .pin3(n7408_2_pin3), .pin13(y_prime), .pin12(n7404_1_pin2),
    .pin11(n7408_2_pin11));  // open: pin4, pin5, pin6, pin10, pin9, pin8
  _7432 #(.ShowInternalStructure("true")) u_7432_1 (
    .pin1(n7408_1_pin3), .pin2(n7408_2_pin11), .pin3(n7432_1_pin3), .pin4(n7408_2_pin11),
    .pin5(n7408_2_pin3), .pin6(n7432_1_pin6), .pin13(n7404_1_pin2), .pin12(n7408_1_pin6),
    .pin11(n7432_1_pin3), .pin10(n7408_1_pin8), .pin9(n7408_1_pin11), .pin8(n7432_1_pin8));
  _7_Segment_Display #(.active("false")) u_7_segment_display_1 (
    .g(in_4), .f(n7432_1_pin3), .a(n7432_1_pin3), .b(n7432_1_pin6), .e(in_4), .d(n7432_1_pin8),
    .c(n7404_1_pin2));  // open: dp

  // Notes on the sheet:
  //   z
  //   y
  //   x
  //   x'
  //   xz
  //   x'z'
  //   x'y'
  //   xy'z
  //   x'y
  //   xy
endmodule
