// Logisim project last.circ as structural Verilog: 1 circuit, main circuit main
module main (
  input  in_1,
  input  in_2,
  input  in_3,
  input  in_4
);

  wire and_1_out, and_2_out, and_3_out, and_4_out, and_5_out, and_6_out, not_1_out, not_2_out, not_3_out,
       or_1_out, or_2_out, or_3_out, or_4_out;

  not not_1 (not_1_out, in_1);
  not not_2 (not_2_out, in_2);
  not not_3 (not_3_out, in_3);
  and and_1 (and_1_out, in_1, in_3);
  and and_2 (and_2_out, not_1_out, in_2);
  or or_1 (or_1_out, not_1_out, in_3);
  and and_3 (and_3_out, in_2, in_3);
  and and_4 (and_4_out, not_1_out, not_3_out);
  and and_5 (and_5_out, not_1_out, not_2_out);
  and and_6 (and_6_out, in_1, not_3_out);
  or or_2 (or_2_out, and_1_out, and_2_out);
  or or_3 (or_3_out, and_5_out, and_6_out);
  or or_4 (or_4_out, and_1_out, and_3_out, and_4_out);
  _7_Segment_Display u_7_segment_display_1 (
    .g(or_1_out), .f(in_4), .a(in_3), .b(or_2_out), .e(in_4), .d(or_3_out), .c(or_4_out));  // open: dp

  // Notes on the sheet:
  //   x
  //   y
  //   z
endmodule
